# Fritzing sketch wiring-diagram (saved by Fritzing 0.9.5d)

parts:
  U1 = ESP32S-HiLetgo [part_number=ESP32S-HiLetgo]
  Relay_5V1 = Keyes Relay [package=THT]
  S2 = SWITCH-MOMENTARY-2 [package=tactile-switch-1101ne]  # not connected

nets:
  N1: U1.GPIO6, Relay_5V1.ground
  N2: U1.GPIO7, Relay_5V1.power
  N3: U1.GPIO8, Relay_5V1.signal

notes:
  Garage Door Switch
  Microusb Power to 5V

custom parts:
  ESP32S-HiLetgo: HiLetgo ESP-WROOM-32 ESP32 ESP-32S Development Board 2.4GHz Dual-Mode WiFi + Bluetooth Dual Cores Microcontroller The ESP32 integrated with Antenna switches, RF Balun, power amplifiers, low-noise amplifiers, filters, and management modules, and the entire solution occupies the least area of PCB. 2.4 GHz Wi-Fi plus Bluetooth dual-mode chip, with TSMC Ultra-low power consumption 40nm technology,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
  Keyes Relay: The Keyes 5V relay module is suitable for SCM development, home appliance control. It uses a 5V~12V TIL control signal which can control DC / AC signal.
